// Logisim project ALU.circ as structural Verilog: 1 circuit, main circuit ALU
module ALU (
  input  [31:0] A,
  input  [31:0] B,
  input  [4:0] Shift,
  input  [3:0] Codop,
  input  CarryIn,
  output [31:0] S,
  output [3:0] Flags
);

  wire and_4_out, and_5_out, and_8_out, and_9_out, bitselector_1_out, bitselector_2_out, bitselector_3_out,
       bitselector_4_out, bitselector_5_out, bitselector_6_out, bitselector_8_out, bitselector_9_out,
       bitselector_10_out, bitselector_11_out, bitselector_12_out, bitselector_13_out, bitselector_14_out,
       bitselector_15_out, bitselector_16_out, bitselector_17_out, bitselector_20_out, bitselector_21_out,
       bitselector_22_out, bitselector_23_out, bitselector_24_out, bitselector_25_out, bitselector_26_out,
       bitselector_27_out, comparator_1_eq, comparator_2_eq, comparator_4_eq, comparator_5_eq, Cout1, Cout2,
       Cout3, Cout4, LSL, LSR, N_out, not_1_out, subtractor_1_bout, subtractor_2_bout, V1, V2, V3, V4,
       xor_2_out, xor_3_out, xor_4_out, xor_5_out, xor_6_out, xor_7_out, xor_8_out, xor_9_out;
  wire [4:0] adder_3_out, subtractor_3_out;
  wire [31:0] ADC, and_1_out, and_3_out, CMN, CMP, multiplier_1_out, negator_1_out, not_2_out, not_3_out,
       or_1_out, R_O_R, SBC, shifter_1_out, shifter_2_out, shifter_3_out, TST, xor_1_out;

  not not_1 (not_1_out, CarryIn);
  assign not_2_out = ~A;  // NOT_Gate not_2, 32 bits wide
  assign not_3_out = ~B;  // NOT_Gate not_3, 32 bits wide
  assign and_1_out = A & B;  // AND_Gate and_1, 32 bits wide
  assign xor_1_out = A ^ B;  // XOR_Gate xor_1, 32 bits wide
  Shifter #(.width(32)) shifter_1 (.in(B), .\dist (Shift), .out(shifter_1_out));
  Shifter #(.shift("lr"), .width(32)) shifter_2 (.in(B), .\dist (Shift), .out(shifter_2_out));
  Shifter #(.shift("ar"), .width(32)) shifter_3 (.in(B), .\dist (Shift), .out(shifter_3_out));
  Adder #(.width(32)) adder_1 (.a(A), .b(B), .out(ADC), .cin(CarryIn), .cout(Cout4));
  Subtractor #(.width(32)) subtractor_1 (.a(B), .b(A), .out(SBC), .bin(not_1_out), .bout(subtractor_1_bout));
  not not_4 (Cout3, subtractor_1_bout);
  Shifter #(.shift("rr"), .width(32)) shifter_4 (.in(B), .\dist (Shift), .out(R_O_R));
  assign TST = A & B;  // AND_Gate and_2, 32 bits wide
  Negator #(.width(32)) negator_1 (.in(A), .out(negator_1_out));
  Subtractor #(.width(32)) subtractor_2 (.a(B), .b(A), .out(CMP), .bin(1'b0), .bout(subtractor_2_bout));
  Adder #(.width(32)) adder_2 (.a(A), .b(B), .out(CMN), .cin(1'b0), .cout(Cout1));
  assign or_1_out = A | B;  // OR_Gate or_1, 32 bits wide
  Multiplier #(.width(32)) multiplier_1 (.a(A), .b(B), .out(multiplier_1_out));  // open: cin, cout
  assign and_3_out = not_2_out & B;  // AND_Gate and_3, 32 bits wide
  not not_5 (Cout2, subtractor_2_bout);
  Multiplexer #(.enable("false"), .select(4), .width(32)) multiplexer_1 (
    .in0(and_1_out), .in1(xor_1_out), .in2(shifter_1_out), .in3(shifter_2_out), .in4(shifter_3_out),
    .in5(ADC), .in6(SBC), .in7(R_O_R), .in8(B), .in9(negator_1_out), .in10(B), .in11(B), .in12(or_1_out),
    .in13(multiplier_1_out), .in14(and_3_out), .in15(not_3_out), .out(S), .sel(Codop));
  BitSelector #(.width(32)) bitselector_1 (.in(A), .out(bitselector_1_out), .sel({5{1'b1}}));
  BitSelector #(.width(32)) bitselector_2 (.in(B), .out(bitselector_2_out), .sel({5{1'b1}}));
  BitSelector #(.width(32)) bitselector_3 (.in(A), .out(bitselector_3_out), .sel({5{1'b1}}));
  BitSelector #(.width(32)) bitselector_4 (.in(B), .out(bitselector_4_out), .sel({5{1'b1}}));
  BitSelector #(.width(32)) bitselector_5 (.in(ADC), .out(bitselector_5_out), .sel({5{1'b1}}));
  BitSelector #(.width(32)) bitselector_6 (.in(CMN), .out(bitselector_6_out), .sel({5{1'b1}}));
  BitSelector #(.width(32)) bitselector_7 (.in(S), .out(N_out), .sel({5{1'b1}}));
  BitSelector #(.width(32)) bitselector_8 (.in(A), .out(bitselector_8_out), .sel({5{1'b1}}));
  BitSelector #(.width(32)) bitselector_9 (.in(B), .out(bitselector_9_out), .sel({5{1'b1}}));
  xor xor_2 (xor_2_out, bitselector_1_out, bitselector_5_out);
  xor xor_3 (xor_3_out, bitselector_5_out, bitselector_2_out);
  BitSelector #(.width(32)) bitselector_10 (.in(A), .out(bitselector_10_out), .sel({5{1'b1}}));
  BitSelector #(.width(32)) bitselector_11 (.in(B), .out(bitselector_11_out), .sel({5{1'b1}}));
  xor xor_4 (xor_4_out, bitselector_3_out, bitselector_6_out);
  xor xor_5 (xor_5_out, bitselector_6_out, bitselector_4_out);
  Comparator #(.width(1)) comparator_1 (
    .a(bitselector_8_out), .b(bitselector_9_out), .eq(comparator_1_eq));  // open: gt, lt
  and and_4 (and_4_out, xor_2_out, xor_3_out);
  Comparator #(.width(1)) comparator_2 (
    .a(bitselector_10_out), .b(bitselector_11_out), .eq(comparator_2_eq));  // open: gt, lt
  and and_5 (and_5_out, xor_4_out, xor_5_out);
  Comparator #(.width(32)) comparator_3 (.a(S), .b({32{1'b0}}), .eq(Flags[2]));  // open: gt, lt
  and and_6 (V1, comparator_1_eq, and_4_out);
  and and_7 (V2, comparator_2_eq, and_5_out);
  BitSelector #(.width(32)) bitselector_12 (.in(SBC), .out(bitselector_12_out), .sel({5{1'b1}}));
  BitSelector #(.width(32)) bitselector_13 (.in(B), .out(bitselector_13_out), .sel({5{1'b1}}));
  BitSelector #(.width(32)) bitselector_14 (.in(CMP), .out(bitselector_14_out), .sel({5{1'b1}}));
  BitSelector #(.width(32)) bitselector_15 (.in(B), .out(bitselector_15_out), .sel({5{1'b1}}));
  BitSelector #(.width(32)) bitselector_16 (.in(A), .out(bitselector_16_out), .sel({5{1'b1}}));
  BitSelector #(.width(32)) bitselector_17 (.in(A), .out(bitselector_17_out), .sel({5{1'b1}}));
  BitSelector #(.width(32)) bitselector_18 (.in(B), .out(LSR), .sel(subtractor_3_out));
  Subtractor #(.width(5)) subtractor_3 (.a(Shift), .b(5'b00001), .out(subtractor_3_out));  // open: bin, bout
  BitSelector #(.width(32)) bitselector_19 (.in(B), .out(LSL), .sel(adder_3_out));
  Adder #(.width(5)) adder_3 (.a(Shift), .b(5'b00001), .out(adder_3_out));  // open: cin, cout
  BitSelector #(.width(32)) bitselector_20 (.in(TST), .out(bitselector_20_out), .sel({5{1'b1}}));
  BitSelector #(.width(32)) bitselector_21 (.in(CMP), .out(bitselector_21_out), .sel({5{1'b1}}));
  BitSelector #(.width(32)) bitselector_22 (.in(CMN), .out(bitselector_22_out), .sel({5{1'b1}}));
  BitSelector #(.width(32)) bitselector_23 (.in(SBC), .out(bitselector_23_out), .sel({5{1'b1}}));
  BitSelector #(.width(32)) bitselector_24 (.in(B), .out(bitselector_24_out), .sel({5{1'b1}}));
  xor xor_6 (xor_6_out, bitselector_12_out, bitselector_16_out);
  xor xor_7 (xor_7_out, bitselector_16_out, bitselector_13_out);
  BitSelector #(.width(32)) bitselector_25 (.in(CMP), .out(bitselector_25_out), .sel({5{1'b1}}));
  BitSelector #(.width(32)) bitselector_26 (.in(B), .out(bitselector_26_out), .sel({5{1'b1}}));
  xor xor_8 (xor_8_out, bitselector_14_out, bitselector_17_out);
  xor xor_9 (xor_9_out, bitselector_17_out, bitselector_15_out);
  Comparator #(.width(1)) comparator_4 (
    .a(bitselector_23_out), .b(bitselector_24_out), .eq(comparator_4_eq));  // open: gt, lt
  and and_8 (and_8_out, xor_6_out, xor_7_out);
  Comparator #(.width(1)) comparator_5 (
    .a(bitselector_25_out), .b(bitselector_26_out), .eq(comparator_5_eq));  // open: gt, lt
  and and_9 (and_9_out, xor_8_out, xor_9_out);
  and and_10 (V3, comparator_4_eq, and_8_out);
  and and_11 (V4, comparator_5_eq, and_9_out);
  Multiplexer #(.enable("false"), .select(4)) multiplexer_2 (
    .in0(N_out), .in1(N_out), .in2(N_out), .in3(N_out), .in4(N_out), .in5(N_out), .in6(N_out), .in7(N_out),
    .in8(bitselector_20_out), .in9(N_out), .in10(bitselector_21_out), .in11(bitselector_22_out),
    .in12(N_out), .in13(N_out), .in14(N_out), .in15(N_out), .out(Flags[3]), .sel(Codop));
  BitSelector #(.width(32)) bitselector_27 (.in(B), .out(bitselector_27_out), .sel({5{1'b1}}));
  Multiplexer #(.enable("false"), .select(4)) multiplexer_3 (
    .in0(1'b0), .in1(1'b0), .in2(1'b0), .in3(1'b0), .in4(1'b0), .in5(V1), .in6(V3), .in7(1'b0), .in8(1'b0),
    .in9(1'b0), .in10(V4), .in11(V2), .in12(1'b0), .in13(1'b0), .in14(1'b0), .in15(1'b0), .out(Flags[0]),
    .sel(Codop));
  Multiplexer #(.enable("false"), .select(4)) multiplexer_4 (
    .in0(1'b0), .in1(1'b0), .in2(LSL), .in3(LSR), .in4(LSR), .in5(Cout4), .in6(Cout3),
    .in7(bitselector_27_out), .in8(1'b0), .in9(1'b0), .in10(Cout2), .in11(Cout1), .in12(1'b0), .in13(1'b0),
    .in14(1'b0), .in15(1'b0), .out(Flags[1]), .sel(Codop));

  // Other names for the same wires on the sheet: Cin = CarryIn; V = Flags[0]; C = Flags[1]; Z = Flags[2];
  //   N = Flags[3]

  // Notes on the sheet:
  //   Note: for ROR, C = N
  //   Note 2: assume that shift > 0 for LSL and LSR
  //   Constante = 0
endmodule
