// Logisim project Ctl_Conditional.circ as structural Verilog: 2 circuits, main circuit Conditional
module Conditional (
  input  Enable,
  input  [15:0] Instruction,
  input  Z,
  input  C,
  input  N,
  input  V,
  output [10:0] Offset,
  output Verified
);

  wire \bool , decod_1_verified, not_1_out, or_2_out;
  wire [4:0] Bits5;
  wire [10:0] and_1_out, and_2_out, bit_extender_2_out, bit_extender_3_out, bit_extender_4_out,
       bit_extender_5_out, bitselector_1_out, or_1_out;

  BitSelector #(.group(11), .width(16)) bitselector_1 (.in(Instruction), .out(bitselector_1_out), .sel(1'b1));
  Bit_Extender #(.in_width(11), .out_width(5)) bit_extender_1 (.in(bitselector_1_out), .out(Bits5));
  not not_1 (not_1_out, Instruction[12]);
  assign bit_extender_2_out = {{10{Instruction[12]}}, Instruction[12]};  // Bit_Extender bit_extender_2
  assign bit_extender_3_out = {{10{not_1_out}}, not_1_out};  // Bit_Extender bit_extender_3
  Comparator #(.width(5)) comparator_1 (.a(Bits5), .b(5'b11100), .eq(\bool ));  // open: gt, lt
  assign bit_extender_4_out = {{3{Instruction[7]}}, Instruction[7:0]};  // Bit_Extender bit_extender_4
  assign and_1_out = bit_extender_4_out & bit_extender_2_out;  // AND_Gate and_1, 11 bits wide
  assign and_2_out = Instruction[10:0] & bit_extender_3_out;  // AND_Gate and_2, 11 bits wide
  assign or_1_out = and_1_out | and_2_out;  // OR_Gate or_1, 11 bits wide
  Decod decod_1 (.cond(Instruction[11:8]), .Z(Z), .C(C), .N(N), .V(V), .Verified(decod_1_verified));
  assign bit_extender_5_out = {{10{Enable}}, Enable};  // Bit_Extender bit_extender_5
  or or_2 (or_2_out, decod_1_verified, \bool );
  assign Offset = or_1_out & bit_extender_5_out;  // AND_Gate and_3, 11 bits wide
  and and_4 (Verified, or_2_out, Enable);

  // Other names for the same wires on the sheet: Cond[3:0] = Instruction[11:8]; Imm11[10:0] = Instruction[10:0];
  //   Imm8[7:0] = Instruction[7:0]; IsCondi = Instruction[12]
endmodule

module Decod (
  input  [3:0] cond,
  input  Z,
  input  C,
  input  N,
  input  V,
  output Verified
);

  wire and_1_out, and_2_out, and_3_out, and_4_out, and_5_out, and_6_out, and_7_out, and_8_out, and_9_out,
       and_10_out, and_11_out, and_12_out, and_13_out, and_14_out, and_15_out, and_16_out, and_17_out,
       and_18_out, and_19_out, and_20_out, not_1_out, not_2_out, not_3_out, not_4_out, not_5_out, not_6_out,
       not_7_out, not_8_out;

  not not_1 (not_1_out, cond[3]);
  not not_2 (not_2_out, cond[2]);
  not not_3 (not_3_out, cond[1]);
  not not_4 (not_4_out, cond[0]);
  not not_5 (not_5_out, Z);
  not not_6 (not_6_out, C);
  not not_7 (not_7_out, N);
  not not_8 (not_8_out, V);
  and and_1 (and_1_out, not_1_out, not_2_out, not_3_out, not_4_out, Z);
  and and_2 (and_2_out, not_1_out, not_2_out, not_3_out, cond[0], not_5_out);
  and and_3 (and_3_out, not_2_out, not_3_out, cond[0], not_5_out, not_6_out);
  and and_4 (and_4_out, not_1_out, not_2_out, cond[1], not_4_out, C);
  and and_5 (and_5_out, not_1_out, not_2_out, cond[1], cond[0], not_6_out);
  and and_6 (and_6_out, not_1_out, cond[2], not_3_out, not_4_out, N);
  and and_7 (and_7_out, cond[2], not_4_out, not_5_out, N, V);
  and and_8 (and_8_out, not_1_out, cond[2], not_3_out, cond[0], not_7_out);
  and and_9 (and_9_out, cond[2], not_3_out, cond[0], not_7_out, V);
  and and_10 (and_10_out, cond[2], cond[1], not_4_out, V);
  and and_11 (and_11_out, not_1_out, cond[2], cond[1], cond[0], not_8_out);
  and and_12 (and_12_out, cond[3], not_2_out, not_3_out, not_4_out, not_5_out, C);
  and and_13 (and_13_out, cond[3], not_3_out, cond[0], Z);
  and and_14 (and_14_out, cond[3], cond[1], not_4_out, not_7_out, not_8_out);
  and and_15 (and_15_out, cond[3], cond[1], not_4_out, N, V);
  and and_16 (and_16_out, cond[3], not_2_out, cond[1], cond[0], not_7_out, V);
  and and_17 (and_17_out, cond[3], not_2_out, cond[1], cond[0], N, not_8_out);
  and and_18 (and_18_out, cond[3], cond[2], not_4_out, not_5_out, not_7_out, not_8_out);
  and and_19 (and_19_out, cond[3], cond[2], not_3_out, cond[0], N, not_8_out);
  and and_20 (and_20_out, cond[3], cond[2], cond[1], not_4_out);
  or or_1 (Verified, and_1_out, and_2_out, and_3_out, and_4_out, and_5_out, and_6_out, and_7_out, and_8_out, and_9_out, and_10_out, and_11_out, and_12_out, and_13_out, and_14_out, and_15_out, and_16_out, and_17_out, and_18_out, and_19_out, and_20_out);
endmodule
