// Logisim project Ctl_Flags_APSR.circ as structural Verilog: 1 circuit, main circuit Flags_APSR
module Flags_APSR (
  input  [3:0] Update_Mask,
  input  [3:0] Flags_In,
  input  Clk,
  input  Rst,
  output [3:0] Flags_Out
);

  wire not_1_out, not_2_out, not_3_out, not_4_out;
  wire [3:0] Bitreuni;

  not not_1 (not_1_out, Flags_In[0]);
  not not_2 (not_2_out, Flags_In[1]);
  not not_3 (not_3_out, Flags_In[2]);
  not not_4 (not_4_out, Flags_In[3]);
  Register #(.width(4)) register_1 (.D(Bitreuni), .clk(Clk), .Q(Flags_Out), .clr(Rst));  // open: en
  Multiplexer #(.enable("false")) multiplexer_1 (
    .in0(Flags_In[0]), .in1(not_1_out), .out(Bitreuni[0]), .sel(Update_Mask[0]));
  Multiplexer #(.enable("false")) multiplexer_2 (
    .in0(Flags_In[1]), .in1(not_2_out), .out(Bitreuni[1]), .sel(Update_Mask[1]));
  Multiplexer #(.enable("false")) multiplexer_3 (
    .in0(Flags_In[2]), .in1(not_3_out), .out(Bitreuni[2]), .sel(Update_Mask[2]));
  Multiplexer #(.enable("false")) multiplexer_4 (
    .in0(Flags_In[3]), .in1(not_4_out), .out(Bitreuni[3]), .sel(Update_Mask[3]));

  // Other names for the same wires on the sheet: FlBit1 = Bitreuni[0]; FlBit2 = Bitreuni[1]; FlBit3 = Bitreuni[2];
  //   FlBit4 = Bitreuni[3]; FBit1 = Flags_In[0]; FBit2 = Flags_In[1]; FBit3 = Flags_In[2]; FBit4 = Flags_In[3];
  //   UBit1 = Update_Mask[0]; UBit2 = Update_Mask[1]; UBit3 = Update_Mask[2]; UBit4 = Update_Mask[3]
endmodule
