// Logisim project Ctl_Load_StoreV1.circ as structural Verilog: 1 circuit, main circuit Load_Store
module Load_Store (
  input  [15:0] Instruction,
  input  Enable,
  input  Clk,
  input  Reset,
  input  [31:0] Stack_Pointer,
  output Store,
  output Load,
  output PC_Hold,
  output [2:0] Rmd,
  output [31:0] RAM_Addr
);

  wire a11bit, d_ff_1_q, Load_Store_Output, not_1_out, xor_1_out;
  wire [2:0] bit_extender_3_out, bit_extender_4_out;
  wire [3:0] bitselector_3_out;
  wire [7:0] bitselector_1_out;
  wire [31:0] bit_extender_2_out, imm8, Ram_Addr_t;

  Adder #(.width(32)) adder_1 (.a(imm8), .b(Stack_Pointer), .out(Ram_Addr_t));  // open: cin, cout
  BitSelector #(.group(8), .width(16)) bitselector_1 (.in(Instruction), .out(bitselector_1_out), .sel(1'b0));
  BitSelector #(.width(16)) bitselector_2 (.in(Instruction), .out(a11bit), .sel(4'b1011));
  and and_1 (Load_Store_Output, a11bit, 1'b1);
  xor xor_1 (xor_1_out, d_ff_1_q, Load_Store_Output);
  assign imm8 = {{24{bitselector_1_out[7]}}, bitselector_1_out};  // Bit_Extender bit_extender_1
  D_Flip_Flop d_ff_1 (.D(xor_1_out), .clk(Clk), .Q(d_ff_1_q), .reset(Reset));  // open: Qn, preset
  and and_2 (PC_Hold, Enable, d_ff_1_q);
  assign bit_extender_2_out = {{31{Enable}}, Enable};  // Bit_Extender bit_extender_2
  and and_3 (Load, Enable, Load_Store_Output);
  not not_1 (not_1_out, Load_Store_Output);
  Bit_Extender #(.in_width(4), .out_width(3)) bit_extender_3 (.in(bitselector_3_out), .out(bit_extender_3_out));
  BitSelector #(.group(4), .width(16)) bitselector_3 (.in(Instruction), .out(bitselector_3_out), .sel(2'b10));
  assign RAM_Addr = bit_extender_2_out & Ram_Addr_t;  // AND_Gate and_4, 32 bits wide
  and and_5 (Store, Enable, not_1_out);
  assign bit_extender_4_out = {{2{Enable}}, Enable};  // Bit_Extender bit_extender_4
  assign Rmd = bit_extender_4_out & bit_extender_3_out;  // AND_Gate and_6, 3 bits wide

  // Other names for the same wires on the sheet: clock = Clk; enableOut = Enable; Load_output = Load;
  //   Pc_Hold_Output = PC_Hold; Ram_out[31:0] = RAM_Addr; registreRT[2:0] = Rmd; SP_IN[31:0] = Stack_Pointer;
  //   Store_output = Store

  // Notes on the sheet:
  //   Instruction: pull=down
  //   Delay load and hold PC for 1 cycle for the RAM to send out requested data 
endmodule
