// Logisim project Ctl_SP_Address.circ as structural Verilog: 1 circuit, main circuit SP_Address
module SP_Address (
  input  [31:0] Stack_Pointer,
  input  [15:0] Instruction,
  input  Enable,
  output [31:0] New_Stack_Pointer,
  output Write_Enable
);

  wire bitselector_3_out, not_1_out;
  wire [6:0] bitselector_1_out, bitselector_2_out;
  wire [31:0] adder_1_out, and_1_out, and_2_out, and_3_out, bit_extender_2_out, bit_extender_3_out, boolean,
       Enable32, not_2_out, or_1_out, subtractor_1_out;

  BitSelector #(.group(7), .width(16)) bitselector_1 (.in(Instruction), .out(bitselector_1_out), .sel(2'b00));
  BitSelector #(.group(7), .width(16)) bitselector_2 (.in(Instruction), .out(bitselector_2_out), .sel(2'b00));
  assign Enable32 = {{31{Enable}}, Enable};  // Bit_Extender bit_extender_1
  not not_1 (not_1_out, bitselector_3_out);
  BitSelector #(.width(16)) bitselector_3 (.in(Instruction), .out(bitselector_3_out), .sel(4'b0111));
  assign bit_extender_2_out = {{25{bitselector_1_out[6]}}, bitselector_1_out};  // Bit_Extender bit_extender_2
  assign bit_extender_3_out = {{25{bitselector_2_out[6]}}, bitselector_2_out};  // Bit_Extender bit_extender_3
  assign boolean = {{31{not_1_out}}, not_1_out};  // Bit_Extender bit_extender_4
  Adder #(.width(32)) adder_1 (.a(Stack_Pointer), .b(bit_extender_2_out), .out(adder_1_out));  // open: cin, cout
  assign not_2_out = ~boolean;  // NOT_Gate not_2, 32 bits wide
  Subtractor #(.width(32)) subtractor_1 (
    .a(Stack_Pointer), .b(bit_extender_3_out), .out(subtractor_1_out));  // open: bin, bout
  assign and_1_out = boolean & adder_1_out;  // AND_Gate and_1, 32 bits wide
  assign and_2_out = not_2_out & subtractor_1_out;  // AND_Gate and_2, 32 bits wide
  assign or_1_out = and_1_out | and_2_out;  // OR_Gate or_1, 32 bits wide
  assign and_3_out = Enable32 & or_1_out;  // AND_Gate and_3, 32 bits wide
  assign New_Stack_Pointer = and_3_out & Enable32;  // AND_Gate and_4, 32 bits wide

  assign Write_Enable = Enable;

  // Notes on the sheet:
  //   Pull output low on Enable = 0
endmodule
