// Logisim project Ctl_Shift_Add_Sub_MovV2.circ as structural Verilog: 3 circuits, main circuit Shift_Add_Sub_Mov
module Shift_Add_Sub_Mov (
  input  Enable,
  input  [15:0] Instruction,
  output [3:0] Flags_Update_Mask,
  output Carry,
  output Imm32_Enable,
  output [2:0] Rm,
  output [2:0] Rn,
  output [2:0] Rd,
  output [4:0] Imm5,
  output [31:0] Imm32,
  output [3:0] ALU_Opcode
);

  wire Add_imm8, Add_Immediate, Add_OR_Sub_Register, Add_Register, Add_Sub_bool, Add_Sub_Imm3_Bool,
       and_38_out, and_39_out, and_40_out, and_41_out, and_42_out, and_43_out, and_44_out, and_46_out,
       and_47_out, and_48_out, and_49_out, and_50_out, and_51_out, and_52_out, and_53_out, and_54_out,
       and_55_out, and_56_out, and_57_out, and_58_out, and_59_out, and_60_out, and_61_out, and_72_out,
       and_73_out, and_74_out, and_75_out, and_76_out, and_77_out, Arithmetic_Shift_Right_bool,
       bit_sortant_decallage_left_logic, bit_sortant_decallage_right_logic, bitselector_27_out,
       bitselector_28_out, C_Flag_Value, Carry_Out, Cmp_Immediate, comparator_7_eq, comparator_8_eq,
       comparator_21_eq, comparator_22_eq, comparator_23_eq, comparator_24_eq, comparator_25_eq,
       comparator_26_eq, comparator_27_eq, comparator_28_eq, comparator_29_eq, comparator_30_eq, Imm8_Codop,
       Imm32_Enable_t, Logical_Shift_Left_bool, Logical_Shift_Right_bool, Mov_Cmp_Imm8_Codop_Bool,
       Mov_Immediate, Move_Codop, or_10_out, Out_Shift_C_Flag, Shift_Add_Sub_Codop_Bool, Shift_bool,
       Shift_Codop, Sub_imm8, Sub_Immediate, Sub_Register;
  wire [1:0] bit_extender_9_out, bit_extender_10_out, bit_extender_11_out, bit_extender_12_out,
       bit_extender_13_out, bit_extender_14_out, bit_extender_15_out, bit_extender_16_out,
       bit_extender_17_out, bit_extender_18_out, bit_extender_19_out, bit_extender_20_out,
       bit_extender_21_out, bit_extender_22_out;
  wire [2:0] Add_Immediate_output, Add_Register_output, adder_1_out, adder_2_out, and_5_out, and_8_out,
       and_9_out, and_10_out, and_11_out, and_12_out, and_13_out, and_14_out, and_17_out, and_18_out,
       and_19_out, and_20_out, and_21_out, and_22_out, and_64_out, and_65_out, bit_extender_7_out,
       bit_extender_8_out, bit_extender_23_out, bit_extender_24_out, bit_extender_32_out,
       bit_extender_33_out, bit_extender_35_out, bit_extender_36_out, bit_extender_37_out,
       bit_extender_38_out, bit_extender_39_out, bit_extender_40_out, bit_extender_41_out,
       bit_extender_42_out, bit_extender_46_out, bit_extender_47_out, bit_extender_48_out,
       bit_extender_49_out, bit_extender_50_out, bit_extender_51_out, bit_extender_52_out,
       bit_extender_53_out, bit_extender_58_out, bit_extender_59_out, bit_extender_60_out,
       bit_extender_61_out, bit_extender_62_out, bit_extender_63_out, bit_extender_68_out,
       bit_extender_69_out, bit_extender_70_out, bit_extender_71_out, bit_extender_72_out,
       bit_extender_76_out, bit_extender_77_out, bitselector_15_out, bitselector_16_out, bitselector_17_out,
       bitselector_18_out, Codop, Get_Rd, left_logical_shift_output, Move_Rd_Out, not_1_out,
       Out_Add_Subb_for_RD, Out_Shift_for_RD, output_for_RD, output_for_RD_Flag, Rd_Move_In, Rd_Shift_In,
       right_arithmetic_shift_output, right_logical_shift_output, Rm_For_Add_Sub_Out, Rm_For_Add_Value,
       Rm_Value_Shift, Rn_For_Add_Sub_Out, Rn_For_Shift_Out, Rn_out, Rn_Value, Shift_Rd_Out,
       Sub_Immediate_output, Sub_Register_output, subtractor_3_out, subtractor_4_out;
  wire [3:0] and_69_out, and_70_out, and_71_out, bit_extender_78_out, bit_extender_79_out,
       bit_extender_80_out, bitselector_5_out, Codeop;
  wire [3:2] Flag_Output;
  wire [4:0] ALU_Opcode_t, bit_extender_1_out, bit_extender_2_out, bit_extender_73_out, bit_extender_74_out,
       bit_extender_75_out, Imm3_To_Imm5_Output, Imm5_Output, Imm5_Shift_Output, imm5_Value,
       subtractor_1_out, subtractor_2_out;
  wire [5:0] bitselector_3_out;
  wire [7:0] Add_imm8_output, adder_3_out, and_6_out, and_7_out, and_15_out, and_16_out, and_23_out,
       and_25_out, and_26_out, and_27_out, and_78_out, bit_extender_29_out, bit_extender_30_out,
       bit_extender_31_out, bit_extender_34_out, bit_extender_43_out, bit_extender_44_out,
       bit_extender_45_out, bit_extender_54_out, bit_extender_55_out, bit_extender_56_out,
       bit_extender_57_out, bit_extender_64_out, bit_extender_65_out, bit_extender_66_out,
       bit_extender_67_out, bit_extender_81_out, bitselector_26_out, Cmp_Immediate_output, Imm8_Mov,
       Mov_Immediate_output, Out_Mov_CMP_For_RD, Sub_imm8_output, subtractor_5_out, subtractor_6_out;
  wire [8:0] bitselector_6_out;
  wire [10:0] bitselector_7_out, bitselector_11_out, bitselector_12_out, bitselector_13_out,
       bitselector_14_out, bitselector_19_out, bitselector_20_out, bitselector_21_out, bitselector_22_out;
  wire [12:0] bitselector_9_out, bitselector_10_out;
  wire [31:0] bit_extender_26_out, bit_extender_27_out, bit_extender_28_out, Imm32_Out, shifter_1_out,
       shifter_2_out, shifter_3_out;

  BitSelector #(.group(3), .width(16)) bitselector_1 (.in(Instruction), .out(Rm_Value_Shift), .sel(3'b001));
  BitSelector #(.group(3), .width(16)) bitselector_2 (.in(Instruction), .out(Rn_Value), .sel(3'b001));
  BitSelector #(.group(6), .width(16)) bitselector_3 (.in(Instruction), .out(bitselector_3_out), .sel(2'b01));
  BitSelector #(.group(8), .width(16)) bitselector_4 (.in(Instruction), .out(Imm8_Mov), .sel(1'b0));
  BitSelector #(.group(4), .width(16)) bitselector_5 (.in(Instruction), .out(bitselector_5_out), .sel(2'b10));
  BitSelector #(.group(9), .width(16)) bitselector_6 (.in(Instruction), .out(bitselector_6_out), .sel(1'b1));
  BitSelector #(.group(11), .width(16)) bitselector_7 (.in(Instruction), .out(bitselector_7_out), .sel(1'b1));
  assign bit_extender_1_out = {{2{1'b0}}, 3'b011};  // Bit_Extender bit_extender_1
  assign bit_extender_2_out = {{2{1'b0}}, 3'b001};  // Bit_Extender bit_extender_2
  Bit_Extender #(.in_width(6), .out_width(5)) bit_extender_3 (.in(bitselector_3_out), .out(imm5_Value));
  BitSelector #(.group(3), .width(16)) bitselector_8 (.in(Instruction), .out(Rm_For_Add_Value), .sel(3'b010));
  Bit_Extender #(.in_width(4), .out_width(3)) bit_extender_4 (.in(bitselector_5_out), .out(Get_Rd));
  Bit_Extender #(.in_width(9), .out_width(3)) bit_extender_5 (.in(bitselector_6_out), .out(Codop));
  Bit_Extender #(.in_width(11), .out_width(5)) bit_extender_6 (.in(bitselector_7_out), .out(ALU_Opcode_t));
  BitSelector #(.group(13), .width(16)) bitselector_9 (.in(Instruction), .out(bitselector_9_out), .sel(1'b1));
  BitSelector #(.group(13), .width(16)) bitselector_10 (.in(Instruction), .out(bitselector_10_out), .sel(1'b1));
  BitSelector #(.group(11), .width(16)) bitselector_11 (.in(Instruction), .out(bitselector_11_out), .sel(1'b1));
  BitSelector #(.group(11), .width(16)) bitselector_12 (.in(Instruction), .out(bitselector_12_out), .sel(1'b1));
  BitSelector #(.group(11), .width(16)) bitselector_13 (.in(Instruction), .out(bitselector_13_out), .sel(1'b1));
  BitSelector #(.group(11), .width(16)) bitselector_14 (.in(Instruction), .out(bitselector_14_out), .sel(1'b1));
  BitSelector #(.group(3), .width(16)) bitselector_15 (.in(Instruction), .out(bitselector_15_out), .sel(3'b011));
  BitSelector #(.group(3), .width(16)) bitselector_16 (.in(Instruction), .out(bitselector_16_out), .sel(3'b011));
  BitSelector #(.group(3), .width(16)) bitselector_17 (.in(Instruction), .out(bitselector_17_out), .sel(3'b011));
  BitSelector #(.group(3), .width(16)) bitselector_18 (.in(Instruction), .out(bitselector_18_out), .sel(3'b011));
  BitSelector #(.group(11), .width(16)) bitselector_19 (.in(Instruction), .out(bitselector_19_out), .sel(1'b1));
  BitSelector #(.group(11), .width(16)) bitselector_20 (.in(Instruction), .out(bitselector_20_out), .sel(1'b1));
  BitSelector #(.group(11), .width(16)) bitselector_21 (.in(Instruction), .out(bitselector_21_out), .sel(1'b1));
  BitSelector #(.group(11), .width(16)) bitselector_22 (.in(Instruction), .out(bitselector_22_out), .sel(1'b1));
  Subtractor #(.width(5)) subtractor_1 (
    .a(bit_extender_1_out), .b(imm5_Value), .out(subtractor_1_out));  // open: bin, bout
  Subtractor #(.width(5)) subtractor_2 (
    .a(imm5_Value), .b(bit_extender_2_out), .out(subtractor_2_out));  // open: bin, bout
  Bit_Extender #(.in_width(13), .out_width(3)) bit_extender_7 (.in(bitselector_9_out), .out(bit_extender_7_out));
  Bit_Extender #(.in_width(13), .out_width(3)) bit_extender_8 (.in(bitselector_10_out), .out(bit_extender_8_out));
  Bit_Extender #(.in_width(11), .out_width(2)) bit_extender_9 (.in(bitselector_11_out), .out(bit_extender_9_out));
  Bit_Extender #(.in_width(11), .out_width(2)) bit_extender_10 (.in(bitselector_12_out), .out(bit_extender_10_out));
  Bit_Extender #(.in_width(11), .out_width(2)) bit_extender_11 (.in(bitselector_13_out), .out(bit_extender_11_out));
  Bit_Extender #(.in_width(11), .out_width(2)) bit_extender_12 (.in(bitselector_14_out), .out(bit_extender_12_out));
  Bit_Extender #(.in_width(3), .out_width(2)) bit_extender_13 (.in(bitselector_15_out), .out(bit_extender_13_out));
  Bit_Extender #(.in_width(3), .out_width(2)) bit_extender_14 (.in(bitselector_16_out), .out(bit_extender_14_out));
  Bit_Extender #(.in_width(3), .out_width(2)) bit_extender_15 (.in(bitselector_17_out), .out(bit_extender_15_out));
  Bit_Extender #(.in_width(3), .out_width(2)) bit_extender_16 (.in(bitselector_18_out), .out(bit_extender_16_out));
  Bit_Extender #(.in_width(11), .out_width(2)) bit_extender_17 (.in(bitselector_19_out), .out(bit_extender_17_out));
  Bit_Extender #(.in_width(11), .out_width(2)) bit_extender_18 (.in(bitselector_20_out), .out(bit_extender_18_out));
  Bit_Extender #(.in_width(11), .out_width(2)) bit_extender_19 (.in(bitselector_21_out), .out(bit_extender_19_out));
  Bit_Extender #(.in_width(11), .out_width(2)) bit_extender_20 (.in(bitselector_22_out), .out(bit_extender_20_out));
  BitSelector #(.width(3)) bitselector_23 (
    .in(Rm_Value_Shift), .out(bit_sortant_decallage_left_logic), .sel(bit_extender_21_out));
  Bit_Extender #(.in_width(5), .out_width(2)) bit_extender_21 (.in(subtractor_1_out), .out(bit_extender_21_out));
  BitSelector #(.width(3)) bitselector_24 (
    .in(Rm_Value_Shift), .out(bit_sortant_decallage_right_logic), .sel(bit_extender_22_out));
  Bit_Extender #(.in_width(5), .out_width(2)) bit_extender_22 (.in(subtractor_2_out), .out(bit_extender_22_out));
  Comparator #(.width(3)) comparator_1 (.a(bit_extender_7_out), .b(3'b001), .eq(Imm8_Codop));  // open: gt, lt
  Comparator #(.width(3)) comparator_2 (.a(bit_extender_8_out), .b(3'b000), .eq(Shift_Codop));  // open: gt, lt
  Comparator #(.width(2)) comparator_3 (
    .a(bit_extender_9_out), .b(2'b00), .eq(Logical_Shift_Left_bool));  // open: gt, lt
  Comparator #(.width(2)) comparator_4 (
    .a(bit_extender_10_out), .b(2'b01), .eq(Logical_Shift_Right_bool));  // open: gt, lt
  Comparator #(.width(2)) comparator_5 (
    .a(bit_extender_11_out), .b(2'b10), .eq(Arithmetic_Shift_Right_bool));  // open: gt, lt
  Comparator #(.width(2)) comparator_6 (.a(bit_extender_12_out), .b(2'b11), .eq(Add_OR_Sub_Register));  // open: gt, lt
  Comparator #(.width(2)) comparator_7 (.a(bit_extender_13_out), .b(2'b00), .eq(comparator_7_eq));  // open: gt, lt
  Comparator #(.width(2)) comparator_8 (.a(bit_extender_14_out), .b(2'b01), .eq(comparator_8_eq));  // open: gt, lt
  Comparator #(.width(2)) comparator_9 (.a(bit_extender_15_out), .b(2'b10), .eq(Add_Immediate));  // open: gt, lt
  Comparator #(.width(2)) comparator_10 (.a(bit_extender_16_out), .b(2'b11), .eq(Sub_Immediate));  // open: gt, lt
  Comparator #(.width(2)) comparator_11 (.a(bit_extender_17_out), .b(2'b00), .eq(Mov_Immediate));  // open: gt, lt
  Comparator #(.width(2)) comparator_12 (.a(bit_extender_18_out), .b(2'b01), .eq(Cmp_Immediate));  // open: gt, lt
  Comparator #(.width(2)) comparator_13 (.a(bit_extender_19_out), .b(2'b10), .eq(Add_imm8));  // open: gt, lt
  Comparator #(.width(2)) comparator_14 (.a(bit_extender_20_out), .b(2'b11), .eq(Sub_imm8));  // open: gt, lt
  and and_1 (Add_Register, Add_OR_Sub_Register, comparator_7_eq);
  and and_2 (Sub_Register, Add_OR_Sub_Register, comparator_8_eq);
  BitSelector #(.group(3), .width(16)) bitselector_25 (.in(Instruction), .out(Rd_Shift_In), .sel(3'b000));
  BitSelector #(.group(8), .width(16)) bitselector_26 (.in(Instruction), .out(bitselector_26_out), .sel(1'b1));
  assign Rd = Shift_Rd_Out | Move_Rd_Out;  // OR_Gate or_1, 3 bits wide
  assign bit_extender_23_out = {{2{Shift_Codop}}, Shift_Codop};  // Bit_Extender bit_extender_23
  assign Shift_Rd_Out = bit_extender_23_out & Rd_Shift_In;  // AND_Gate and_3, 3 bits wide
  assign bit_extender_24_out = {{2{Move_Codop}}, Move_Codop};  // Bit_Extender bit_extender_24
  assign Move_Rd_Out = bit_extender_24_out & Rd_Move_In;  // AND_Gate and_4, 3 bits wide
  Bit_Extender #(.out_width(3)) bit_extender_25 (.in(bitselector_26_out), .out(Rd_Move_In));
  BitSelector #(.width(16)) bitselector_27 (.in(Instruction), .out(bitselector_27_out), .sel(4'b1101));
  BitSelector #(.width(16)) bitselector_28 (.in(Instruction), .out(bitselector_28_out), .sel(4'b1101));
  Comparator #(.width(1)) comparator_15 (.a(bitselector_27_out), .b(1'b0), .eq(Shift_Codop));  // open: gt, lt
  Comparator #(.width(1)) comparator_16 (.a(bitselector_28_out), .b(1'b1), .eq(Move_Codop));  // open: gt, lt
  Comparator #(.width(3)) comparator_17 (.a(Codop), .b(3'b000), .eq(Shift_Add_Sub_Codop_Bool));  // open: gt, lt
  Comparator #(.width(3)) comparator_18 (.a(Codop), .b(3'b001), .eq(Mov_Cmp_Imm8_Codop_Bool));  // open: gt, lt
  ALU_Opcode_Calculator alu_opcode_calculator_1 (.AluOpcode(ALU_Opcode_t), .Codop(ALU_Opcode));
  Flag_Calculator flag_calculator_1 (.AluOpcode(ALU_Opcode), .Flag(Flags_Update_Mask));
  assign bit_extender_26_out = {{29{Rm_Value_Shift[2]}}, Rm_Value_Shift};  // Bit_Extender bit_extender_26
  Shifter #(.width(32)) shifter_1 (.in(bit_extender_26_out), .\dist (imm5_Value), .out(shifter_1_out));
  assign bit_extender_27_out = {{29{Rm_Value_Shift[2]}}, Rm_Value_Shift};  // Bit_Extender bit_extender_27
  assign bit_extender_28_out = {{29{Rm_Value_Shift[2]}}, Rm_Value_Shift};  // Bit_Extender bit_extender_28
  Adder #(.width(3)) adder_1 (.a(Rn_Value), .b(Rm_For_Add_Value), .out(adder_1_out));  // open: cin, cout
  assign bit_extender_29_out = {{5{Get_Rd[2]}}, Get_Rd};  // Bit_Extender bit_extender_29
  assign bit_extender_30_out = {{5{Get_Rd[2]}}, Get_Rd};  // Bit_Extender bit_extender_30
  assign bit_extender_31_out = {{5{Get_Rd[2]}}, Get_Rd};  // Bit_Extender bit_extender_31
  assign bit_extender_32_out = {{2{Logical_Shift_Left_bool}}, Logical_Shift_Left_bool};  // Bit_Extender bit_extender_32
  Bit_Extender #(.in_width(32), .out_width(3)) bit_extender_33 (.in(shifter_1_out), .out(bit_extender_33_out));
  Shifter #(.shift("lr"), .width(32)) shifter_2 (.in(bit_extender_27_out), .\dist (imm5_Value), .out(shifter_2_out));
  Shifter #(.shift("ar"), .width(32)) shifter_3 (.in(bit_extender_28_out), .\dist (imm5_Value), .out(shifter_3_out));
  Subtractor #(.width(3)) subtractor_3 (.a(Rn_Value), .b(Rm_For_Add_Value), .out(subtractor_3_out));  // open: bin, bout
  Adder #(.width(3)) adder_2 (.a(Rn_Value), .b(Rm_For_Add_Value), .out(adder_2_out));  // open: cin, cout
  Subtractor #(.width(3)) subtractor_4 (.a(Rn_Value), .b(Rm_For_Add_Value), .out(subtractor_4_out));  // open: bin, bout
  assign bit_extender_34_out = {{7{Mov_Immediate}}, Mov_Immediate};  // Bit_Extender bit_extender_34
  Subtractor subtractor_5 (.a(bit_extender_29_out), .b(Imm8_Mov), .out(subtractor_5_out));  // open: bin, bout
  Adder adder_3 (.a(bit_extender_30_out), .b(Imm8_Mov), .out(adder_3_out));  // open: cin, cout
  Subtractor subtractor_6 (.a(bit_extender_31_out), .b(Imm8_Mov), .out(subtractor_6_out));  // open: bin, bout
  assign and_5_out = bit_extender_32_out & bit_extender_33_out;  // AND_Gate and_5, 3 bits wide
  assign bit_extender_35_out = {{2{Logical_Shift_Right_bool}}, Logical_Shift_Right_bool};  // Bit_Extender bit_extender_35
  Bit_Extender #(.in_width(32), .out_width(3)) bit_extender_36 (.in(shifter_2_out), .out(bit_extender_36_out));
  assign bit_extender_37_out = {{2{Arithmetic_Shift_Right_bool}}, Arithmetic_Shift_Right_bool};  // Bit_Extender bit_extender_37
  Bit_Extender #(.in_width(32), .out_width(3)) bit_extender_38 (.in(shifter_3_out), .out(bit_extender_38_out));
  assign bit_extender_39_out = {{2{Add_Register}}, Add_Register};  // Bit_Extender bit_extender_39
  assign bit_extender_40_out = {{2{Sub_Register}}, Sub_Register};  // Bit_Extender bit_extender_40
  assign bit_extender_41_out = {{2{Add_Immediate}}, Add_Immediate};  // Bit_Extender bit_extender_41
  assign bit_extender_42_out = {{2{Sub_Immediate}}, Sub_Immediate};  // Bit_Extender bit_extender_42
  assign and_6_out = bit_extender_34_out & Imm8_Mov;  // AND_Gate and_6, 8 bits wide
  assign bit_extender_43_out = {{7{Cmp_Immediate}}, Cmp_Immediate};  // Bit_Extender bit_extender_43
  assign and_7_out = bit_extender_43_out & subtractor_5_out;  // AND_Gate and_7, 8 bits wide
  assign bit_extender_44_out = {{7{Add_imm8}}, Add_imm8};  // Bit_Extender bit_extender_44
  assign bit_extender_45_out = {{7{Sub_imm8}}, Sub_imm8};  // Bit_Extender bit_extender_45
  assign bit_extender_46_out = {{2{Shift_Codop}}, Shift_Codop};  // Bit_Extender bit_extender_46
  assign and_8_out = bit_extender_46_out & and_5_out;  // AND_Gate and_8, 3 bits wide
  assign and_9_out = bit_extender_35_out & bit_extender_36_out;  // AND_Gate and_9, 3 bits wide
  assign and_10_out = bit_extender_37_out & bit_extender_38_out;  // AND_Gate and_10, 3 bits wide
  assign bit_extender_47_out = {{2{Shift_Codop}}, Shift_Codop};  // Bit_Extender bit_extender_47
  assign and_11_out = bit_extender_39_out & adder_1_out;  // AND_Gate and_11, 3 bits wide
  assign and_12_out = bit_extender_40_out & subtractor_3_out;  // AND_Gate and_12, 3 bits wide
  assign and_13_out = bit_extender_41_out & adder_2_out;  // AND_Gate and_13, 3 bits wide
  assign and_14_out = bit_extender_42_out & subtractor_4_out;  // AND_Gate and_14, 3 bits wide
  assign and_15_out = bit_extender_44_out & adder_3_out;  // AND_Gate and_15, 8 bits wide
  assign and_16_out = bit_extender_45_out & subtractor_6_out;  // AND_Gate and_16, 8 bits wide
  assign bit_extender_48_out = {{2{Enable}}, Enable};  // Bit_Extender bit_extender_48
  assign bit_extender_49_out = {{2{Shift_Codop}}, Shift_Codop};  // Bit_Extender bit_extender_49
  assign and_17_out = bit_extender_49_out & and_9_out;  // AND_Gate and_17, 3 bits wide
  assign bit_extender_50_out = {{2{Shift_Codop}}, Shift_Codop};  // Bit_Extender bit_extender_50
  assign and_18_out = bit_extender_50_out & and_10_out;  // AND_Gate and_18, 3 bits wide
  assign and_19_out = bit_extender_47_out & and_11_out;  // AND_Gate and_19, 3 bits wide
  assign bit_extender_51_out = {{2{Shift_Codop}}, Shift_Codop};  // Bit_Extender bit_extender_51
  assign and_20_out = bit_extender_51_out & and_12_out;  // AND_Gate and_20, 3 bits wide
  assign bit_extender_52_out = {{2{Shift_Codop}}, Shift_Codop};  // Bit_Extender bit_extender_52
  assign and_21_out = bit_extender_52_out & and_13_out;  // AND_Gate and_21, 3 bits wide
  assign bit_extender_53_out = {{2{Shift_Codop}}, Shift_Codop};  // Bit_Extender bit_extender_53
  assign and_22_out = bit_extender_53_out & and_14_out;  // AND_Gate and_22, 3 bits wide
  assign bit_extender_54_out = {{7{Imm8_Codop}}, Imm8_Codop};  // Bit_Extender bit_extender_54
  assign and_23_out = bit_extender_54_out & and_6_out;  // AND_Gate and_23, 8 bits wide
  assign bit_extender_55_out = {{7{Imm8_Codop}}, Imm8_Codop};  // Bit_Extender bit_extender_55
  assign bit_extender_56_out = {{7{Imm8_Codop}}, Imm8_Codop};  // Bit_Extender bit_extender_56
  assign bit_extender_57_out = {{7{Imm8_Codop}}, Imm8_Codop};  // Bit_Extender bit_extender_57
  assign left_logical_shift_output = bit_extender_48_out & and_8_out;  // AND_Gate and_24, 3 bits wide
  assign and_25_out = bit_extender_55_out & and_7_out;  // AND_Gate and_25, 8 bits wide
  assign and_26_out = bit_extender_56_out & and_15_out;  // AND_Gate and_26, 8 bits wide
  assign and_27_out = bit_extender_57_out & and_16_out;  // AND_Gate and_27, 8 bits wide
  assign bit_extender_58_out = {{2{Enable}}, Enable};  // Bit_Extender bit_extender_58
  assign right_logical_shift_output = bit_extender_58_out & and_17_out;  // AND_Gate and_28, 3 bits wide
  assign bit_extender_59_out = {{2{Enable}}, Enable};  // Bit_Extender bit_extender_59
  assign right_arithmetic_shift_output = bit_extender_59_out & and_18_out;  // AND_Gate and_29, 3 bits wide
  assign bit_extender_60_out = {{2{Enable}}, Enable};  // Bit_Extender bit_extender_60
  assign Add_Register_output = bit_extender_60_out & and_19_out;  // AND_Gate and_30, 3 bits wide
  assign bit_extender_61_out = {{2{Enable}}, Enable};  // Bit_Extender bit_extender_61
  assign bit_extender_62_out = {{2{Enable}}, Enable};  // Bit_Extender bit_extender_62
  assign bit_extender_63_out = {{2{Enable}}, Enable};  // Bit_Extender bit_extender_63
  assign bit_extender_64_out = {{7{Enable}}, Enable};  // Bit_Extender bit_extender_64
  assign bit_extender_65_out = {{7{Enable}}, Enable};  // Bit_Extender bit_extender_65
  assign bit_extender_66_out = {{7{Enable}}, Enable};  // Bit_Extender bit_extender_66
  assign bit_extender_67_out = {{7{Enable}}, Enable};  // Bit_Extender bit_extender_67
  assign Sub_Register_output = bit_extender_61_out & and_20_out;  // AND_Gate and_31, 3 bits wide
  assign Add_Immediate_output = bit_extender_62_out & and_21_out;  // AND_Gate and_32, 3 bits wide
  assign Sub_Immediate_output = bit_extender_63_out & and_22_out;  // AND_Gate and_33, 3 bits wide
  assign Mov_Immediate_output = bit_extender_64_out & and_23_out;  // AND_Gate and_34, 8 bits wide
  assign Cmp_Immediate_output = bit_extender_65_out & and_25_out;  // AND_Gate and_35, 8 bits wide
  assign Add_imm8_output = bit_extender_66_out & and_26_out;  // AND_Gate and_36, 8 bits wide
  assign Sub_imm8_output = bit_extender_67_out & and_27_out;  // AND_Gate and_37, 8 bits wide
  Comparator #(.width(3)) comparator_19 (.a(output_for_RD_Flag), .b(3'b000), .lt(Flag_Output[3]));  // open: gt, eq
  Comparator #(.width(3)) comparator_20 (.a(output_for_RD_Flag), .b(3'b000), .eq(Flag_Output[2]));  // open: gt, lt
  and and_38 (and_38_out, Logical_Shift_Left_bool, 1'b1);
  and and_39 (and_39_out, Logical_Shift_Right_bool, 1'b1);
  and and_40 (and_40_out, Arithmetic_Shift_Right_bool, 1'b1);
  or or_2 (C_Flag_Value, Out_Shift_C_Flag, Out_Shift_C_Flag);
  and and_41 (and_41_out, and_38_out, bit_sortant_decallage_left_logic);
  and and_42 (and_42_out, and_39_out, bit_sortant_decallage_right_logic);
  and and_43 (and_43_out, and_40_out, bit_sortant_decallage_right_logic);
  or or_3 (Out_Shift_C_Flag, and_41_out, and_42_out, and_43_out);
  Bit_Extender #(.out_width(3)) bit_extender_68 (.in(Out_Mov_CMP_For_RD), .out(bit_extender_68_out));
  assign output_for_RD_Flag = Out_Shift_for_RD | bit_extender_68_out | Out_Add_Subb_for_RD;  // OR_Gate or_4, 3 bits wide
  assign Out_Mov_CMP_For_RD = Add_imm8_output | Mov_Immediate_output | Cmp_Immediate_output | Sub_imm8_output;  // OR_Gate or_5, 8 bits wide
  assign Out_Shift_for_RD = left_logical_shift_output | right_logical_shift_output | right_arithmetic_shift_output;  // OR_Gate or_6, 3 bits wide
  assign Out_Add_Subb_for_RD = Add_Immediate_output | Add_Register_output | Sub_Register_output | Sub_Immediate_output;  // OR_Gate or_7, 3 bits wide
  assign bit_extender_69_out = {{2{and_44_out}}, and_44_out};  // Bit_Extender bit_extender_69
  and and_44 (and_44_out, Imm8_Codop, Cmp_Immediate);
  assign not_1_out = ~bit_extender_69_out;  // NOT_Gate not_1, 3 bits wide
  assign output_for_RD = not_1_out & output_for_RD_Flag;  // AND_Gate and_45, 3 bits wide
  or or_8 (Add_Sub_Imm3_Bool, Add_Immediate, Sub_Immediate);
  and and_46 (and_46_out, Add_Sub_Imm3_Bool, Shift_Codop);
  and and_47 (and_47_out, Shift_bool, Shift_Codop);
  assign bit_extender_70_out = {{2{and_48_out}}, and_48_out};  // Bit_Extender bit_extender_70
  and and_48 (and_48_out, Shift_bool, Shift_Codop);
  and and_49 (and_49_out, Add_Register, Shift_Codop);
  and and_50 (and_50_out, Sub_Register, Shift_Codop);
  and and_51 (and_51_out, Add_Immediate, Shift_Codop);
  and and_52 (and_52_out, Sub_Immediate, Shift_Codop);
  assign bit_extender_71_out = {{2{Add_Sub_bool}}, Add_Sub_bool};  // Bit_Extender bit_extender_71
  assign bit_extender_72_out = {{2{Add_Sub_bool}}, Add_Sub_bool};  // Bit_Extender bit_extender_72
  and and_53 (and_53_out, Logical_Shift_Left_bool, Shift_Codop);
  and and_54 (and_54_out, Logical_Shift_Right_bool, Shift_Codop);
  and and_55 (and_55_out, Arithmetic_Shift_Right_bool, Shift_Codop);
  and and_56 (and_56_out, Add_Register, Shift_Codop);
  and and_57 (and_57_out, Sub_Register, Shift_Codop);
  and and_58 (and_58_out, Add_Immediate, Shift_Codop);
  and and_59 (and_59_out, Sub_Immediate, Shift_Codop);
  and and_60 (and_60_out, Add_imm8, Imm8_Codop);
  and and_61 (and_61_out, Sub_imm8, Imm8_Codop);
  or or_9 (Shift_bool, Logical_Shift_Left_bool, Logical_Shift_Right_bool, Arithmetic_Shift_Right_bool);
  assign bit_extender_73_out = {{4{and_46_out}}, and_46_out};  // Bit_Extender bit_extender_73
  assign bit_extender_74_out = {{2{1'b0}}, Rm_For_Add_Value};  // Bit_Extender bit_extender_74
  assign bit_extender_75_out = {{4{and_47_out}}, and_47_out};  // Bit_Extender bit_extender_75
  assign Rn_For_Shift_Out = bit_extender_70_out & Rm_Value_Shift;  // AND_Gate and_62, 3 bits wide
  Comparator #(.width(1)) comparator_21 (.a(and_49_out), .b(1'b1), .eq(comparator_21_eq));  // open: gt, lt
  Comparator #(.width(1)) comparator_22 (.a(and_50_out), .b(1'b1), .eq(comparator_22_eq));  // open: gt, lt
  Comparator #(.width(1)) comparator_23 (.a(and_51_out), .b(1'b1), .eq(comparator_23_eq));  // open: gt, lt
  Comparator #(.width(1)) comparator_24 (.a(and_52_out), .b(1'b1), .eq(comparator_24_eq));  // open: gt, lt
  assign Rn_For_Add_Sub_Out = bit_extender_72_out & Rn_Value;  // AND_Gate and_63, 3 bits wide
  assign and_64_out = Rn_For_Shift_Out & bit_extender_76_out;  // AND_Gate and_64, 3 bits wide
  assign bit_extender_76_out = {{2{Shift_bool}}, Shift_bool};  // Bit_Extender bit_extender_76
  assign and_65_out = Rn_For_Add_Sub_Out & bit_extender_77_out;  // AND_Gate and_65, 3 bits wide
  assign bit_extender_77_out = {{2{Add_Sub_bool}}, Add_Sub_bool};  // Bit_Extender bit_extender_77
  assign bit_extender_78_out = {{3{and_53_out}}, and_53_out};  // Bit_Extender bit_extender_78
  assign bit_extender_79_out = {{3{and_54_out}}, and_54_out};  // Bit_Extender bit_extender_79
  assign bit_extender_80_out = {{3{and_55_out}}, and_55_out};  // Bit_Extender bit_extender_80
  Comparator #(.width(1)) comparator_25 (.a(and_56_out), .b(1'b1), .eq(comparator_25_eq));  // open: gt, lt
  Comparator #(.width(1)) comparator_26 (.a(and_57_out), .b(1'b1), .eq(comparator_26_eq));  // open: gt, lt
  Comparator #(.width(1)) comparator_27 (.a(and_58_out), .b(1'b1), .eq(comparator_27_eq));  // open: gt, lt
  Comparator #(.width(1)) comparator_28 (.a(and_59_out), .b(1'b1), .eq(comparator_28_eq));  // open: gt, lt
  Comparator #(.width(1)) comparator_29 (.a(and_60_out), .b(1'b1), .eq(comparator_29_eq));  // open: gt, lt
  Comparator #(.width(1)) comparator_30 (.a(and_61_out), .b(1'b1), .eq(comparator_30_eq));  // open: gt, lt
  or or_10 (or_10_out, Mov_Immediate, Cmp_Immediate, Add_imm8, Sub_imm8);
  assign bit_extender_81_out = {{7{Imm32_Enable_t}}, Imm32_Enable_t};  // Bit_Extender bit_extender_81
  assign Imm3_To_Imm5_Output = bit_extender_73_out & bit_extender_74_out;  // AND_Gate and_66, 5 bits wide
  assign Imm5_Shift_Output = bit_extender_75_out & imm5_Value;  // AND_Gate and_67, 5 bits wide
  or or_11 (Add_Sub_bool, comparator_21_eq, comparator_22_eq, comparator_23_eq, comparator_24_eq);
  assign Rm_For_Add_Sub_Out = bit_extender_71_out & Rm_For_Add_Value;  // AND_Gate and_68, 3 bits wide
  assign Rn_out = and_64_out | and_65_out;  // OR_Gate or_12, 3 bits wide
  assign and_69_out = bit_extender_78_out & 4'b0010;  // AND_Gate and_69, 4 bits wide
  assign and_70_out = bit_extender_79_out & 4'b0011;  // AND_Gate and_70, 4 bits wide
  assign and_71_out = bit_extender_80_out & 4'b0100;  // AND_Gate and_71, 4 bits wide
  and and_72 (and_72_out, comparator_25_eq, 1'b0);
  and and_73 (and_73_out, comparator_26_eq, 1'b1);
  and and_74 (and_74_out, comparator_27_eq, 1'b0);
  and and_75 (and_75_out, comparator_28_eq, 1'b1);
  and and_76 (and_76_out, comparator_29_eq, 1'b0);
  and and_77 (and_77_out, comparator_30_eq, 1'b1);
  assign and_78_out = bit_extender_81_out & Imm8_Mov;  // AND_Gate and_78, 8 bits wide
  assign Imm5_Output = Imm5_Shift_Output | Imm3_To_Imm5_Output;  // OR_Gate or_13, 5 bits wide
  assign Codeop = and_69_out | and_70_out | and_71_out;  // OR_Gate or_14, 4 bits wide
  or or_15 (Carry_Out, and_72_out, and_73_out, and_74_out, and_75_out, and_76_out, and_77_out);
  and and_79 (Imm32_Enable_t, or_10_out, Imm8_Codop);
  assign Imm32_Out = {{24{1'b0}}, and_78_out};  // Bit_Extender bit_extender_82

  // Other names for the same wires on the sheet: Flag_Out[3:0] = Flags_Update_Mask; Flag_Output[1] = C_Flag_Value;
  //   Z_Flag_Value = Flag_Output[2]; N_Flag_Value = Flag_Output[3]; Opcode[3:0] = ALU_Opcode; Rd_Out[2:0] = Rd

  // Notes on the sheet:
  //   Note: ALU uses Rn register for shifts. Use Rn instead of Rm for shifts (immediate) here too
  //   Note 3: Imm32_Enable forces the use of the immediate for Rm register
  //   Note 2: MOV uses RSB ALU opcode with Imm8 reversed so that it is copied to output register
  //   Pull output low on Enable = 0
  //   only ADD and SUB use Rm
  //   Enable carry for SUB since it is reversed in ALU
  //   ALU will use Imm32 instead of Rm
endmodule

module ALU_Opcode_Calculator (
  input  [4:0] AluOpcode,
  output [3:0] Codop
);

  wire and_2_out, and_3_out, and_4_out, and_5_out, and_6_out, and_7_out, not_1_out, not_2_out, not_3_out,
       not_4_out;

  not not_1 (not_1_out, AluOpcode[4]);
  not not_2 (not_2_out, AluOpcode[3]);
  not not_3 (not_3_out, AluOpcode[2]);
  not not_4 (not_4_out, AluOpcode[0]);
  and and_1 (Codop[3], AluOpcode[4], not_2_out);
  and and_2 (and_2_out, not_1_out, not_2_out);
  and and_3 (and_3_out, AluOpcode[2], AluOpcode[0]);
  and and_4 (and_4_out, AluOpcode[4], AluOpcode[2]);
  and and_5 (and_5_out, not_1_out, not_2_out, AluOpcode[2]);
  and and_6 (and_6_out, not_1_out, AluOpcode[2], not_4_out);
  and and_7 (and_7_out, AluOpcode[4], not_3_out);
  or or_1 (Codop[1], and_2_out, and_3_out, and_4_out);
  or or_2 (Codop[0], and_5_out, and_6_out, and_7_out);

  assign Codop[2] = AluOpcode[3];
endmodule

module Flag_Calculator (
  input  [3:0] AluOpcode,
  output [3:0] Flag
);

  wire comparator_1_eq, comparator_2_eq, comparator_3_eq, comparator_4_eq;

  not not_1 (Flag[1], comparator_1_eq);
  Comparator #(.width(4)) comparator_1 (.a(AluOpcode), .b(4'b1001), .eq(comparator_1_eq));  // open: gt, lt
  Comparator #(.width(4)) comparator_2 (.a(AluOpcode), .b(4'b1010), .eq(comparator_2_eq));  // open: gt, lt
  Comparator #(.width(4)) comparator_3 (.a(AluOpcode), .b(4'b0101), .eq(comparator_3_eq));  // open: gt, lt
  Comparator #(.width(4)) comparator_4 (.a(AluOpcode), .b(4'b0110), .eq(comparator_4_eq));  // open: gt, lt
  or or_1 (Flag[0], comparator_2_eq, comparator_3_eq, comparator_4_eq);

  assign Flag[3:2] = 2'b11;

  // Other names for the same wires on the sheet: V_Flag = Flag[0]; C_Flag = Flag[1]; Opcode[3:0] = AluOpcode
endmodule
