// Logisim project ALU.circ as structural Verilog: 1 circuit, main circuit ALU
module ALU (
  input  [31:0] A,
  input  [31:0] B,
  input  [4:0] Shift,
  input  CarryIn,
  output [3:0] Codop,
  output [31:0] S,
  output [3:0] Flags
);

  wire and_3_out, and_4_out, and_7_out, and_8_out, bitselector_1_out, bitselector_2_out, bitselector_3_out,
       bitselector_4_out, bitselector_5_out, bitselector_6_out, bitselector_7_out, bitselector_8_out,
       bitselector_9_out, bitselector_10_out, bitselector_14_out, bitselector_15_out, bitselector_16_out,
       bitselector_17_out, bitselector_18_out, bitselector_19_out, bitselector_20_out, bitselector_21_out,
       bitselector_22_out, bitselector_23_out, CarryInput, comparator_3_eq, comparator_4_eq, comparator_6_eq,
       comparator_7_eq, xor_2_out, xor_3_out, xor_4_out, xor_5_out, xor_6_out, xor_7_out, xor_8_out,
       xor_9_out;
  wire [4:0] subtractor_4_out, subtractor_5_out, subtractor_6_out;
  wire [31:0] ADC, adder_2_out, and_1_out, and_2_out, ASR, CMN, CMP, multiplier_1_out, not_1_out, not_2_out,
       or_1_out, or_2_out, SBC, shifter_1_out, shifter_2_out, shifter_4_out, SignInpout, subtractor_1_out,
       xor_1_out;

  assign and_1_out = A & B;  // AND_Gate and_1, 32 bits wide
  assign xor_1_out = A ^ B;  // XOR_Gate xor_1, 32 bits wide
  Shifter #(.width(32)) shifter_1 (.in(B), .\dist (Shift), .out(shifter_1_out));
  Shifter #(.shift("lr"), .width(32)) shifter_2 (.in(B), .\dist (Shift), .out(shifter_2_out));
  Shifter #(.shift("ar"), .width(32)) shifter_3 (.in(B), .\dist (Shift), .out(ASR));
  Adder #(.width(32)) adder_1 (.a(A), .b(B), .out(ADC), .cin(CarryIn), .cout(CarryInput));
  Adder #(.width(32)) adder_2 (.a(A), .b(B), .out(adder_2_out), .cin(CarryIn));  // open: cout
  Shifter #(.shift("rr"), .width(32)) shifter_4 (.in(B), .\dist (Shift), .out(shifter_4_out));
  assign and_2_out = A & B;  // AND_Gate and_2, 32 bits wide
  Subtractor #(.width(32)) subtractor_1 (
    .a({32{1'b0}}), .b(A), .out(subtractor_1_out), .bout(CarryInput));  // open: bin
  Subtractor #(.width(32)) subtractor_2 (.a(A), .b(B), .out(CMP), .bout(CarryInput));  // open: bin
  Adder #(.width(32)) adder_3 (.a(A), .b(B), .out(CMN), .cout(CarryInput));  // open: cin
  Multiplier #(.width(32)) multiplier_1 (.a(A), .b(B), .out(multiplier_1_out));  // open: cin, cout
  assign not_1_out = ~B;  // NOT_Gate not_1, 32 bits wide
  assign not_2_out = ~B;  // NOT_Gate not_2, 32 bits wide
  assign or_1_out = A | B;  // OR_Gate or_1, 32 bits wide
  assign or_2_out = A | not_1_out;  // OR_Gate or_2, 32 bits wide
  Subtractor #(.width(32)) subtractor_3 (.a(adder_2_out), .b({32{1'b1}}), .out(SBC));  // open: bin, bout
  Multiplexer #(.enable("false"), .select(4), .width(32)) multiplexer_1 (
    .in0(and_1_out), .in1(xor_1_out), .in2(shifter_1_out), .in3(shifter_2_out), .in4(ASR), .in5(ADC),
    .in6(SBC), .in7(shifter_4_out), .in8(and_2_out), .in9(subtractor_1_out), .in10(CMP), .in11(CMN),
    .in12(or_1_out), .in13(multiplier_1_out), .in14(or_2_out), .in15(not_2_out), .out(S), .sel(Codop));
  BitSelector #(.width(32)) bitselector_1 (.in(A), .out(bitselector_1_out), .sel({5{1'b1}}));
  BitSelector #(.width(32)) bitselector_2 (.in(ADC), .out(bitselector_2_out), .sel({5{1'b1}}));
  BitSelector #(.width(32)) bitselector_3 (.in(B), .out(bitselector_3_out), .sel({5{1'b1}}));
  BitSelector #(.width(32)) bitselector_4 (.in(A), .out(bitselector_4_out), .sel({5{1'b1}}));
  BitSelector #(.width(32)) bitselector_5 (.in(CMN), .out(bitselector_5_out), .sel({5{1'b1}}));
  BitSelector #(.width(32)) bitselector_6 (.in(B), .out(bitselector_6_out), .sel({5{1'b1}}));
  Subtractor #(.width(5)) subtractor_4 (.a(Shift), .b(5'b00001), .out(subtractor_4_out));  // open: bin, bout
  Comparator #(.width(1)) comparator_1 (.a(CarryInput), .b(1'b1), .eq(Flags[2]));  // open: gt, lt
  BitSelector #(.width(32)) bitselector_7 (.in(A), .out(bitselector_7_out), .sel({5{1'b1}}));
  BitSelector #(.width(32)) bitselector_8 (.in(B), .out(bitselector_8_out), .sel({5{1'b1}}));
  xor xor_2 (xor_2_out, bitselector_1_out, bitselector_2_out);
  xor xor_3 (xor_3_out, bitselector_2_out, bitselector_3_out);
  BitSelector #(.width(32)) bitselector_9 (.in(A), .out(bitselector_9_out), .sel({5{1'b1}}));
  BitSelector #(.width(32)) bitselector_10 (.in(B), .out(bitselector_10_out), .sel({5{1'b1}}));
  xor xor_4 (xor_4_out, bitselector_4_out, bitselector_5_out);
  xor xor_5 (xor_5_out, bitselector_5_out, bitselector_6_out);
  BitSelector #(.width(32)) bitselector_11 (.in(B), .out(Flags[2]), .sel(subtractor_5_out));
  Subtractor #(.width(5)) subtractor_5 (
    .a({5{1'b1}}), .b(subtractor_4_out), .out(subtractor_5_out));  // open: bin, bout
  BitSelector #(.width(32)) bitselector_12 (.in(ASR), .out(Flags[2]), .sel({5{1'b1}}));
  Comparator #(.width(32)) comparator_2 (.a(S), .b({32{1'b0}}), .eq(Flags[1]), .lt(Flags[0]));  // open: gt
  Comparator #(.width(1)) comparator_3 (
    .a(bitselector_7_out), .b(bitselector_8_out), .eq(comparator_3_eq));  // open: gt, lt
  and and_3 (and_3_out, xor_2_out, xor_3_out);
  Comparator #(.width(1)) comparator_4 (
    .a(bitselector_9_out), .b(bitselector_10_out), .eq(comparator_4_eq));  // open: gt, lt
  and and_4 (and_4_out, xor_4_out, xor_5_out);
  and and_5 (Flags[3], comparator_3_eq, and_3_out);
  and and_6 (Flags[3], comparator_4_eq, and_4_out);
  Subtractor #(.width(5)) subtractor_6 (.a(Shift), .b(5'b00001), .out(subtractor_6_out));  // open: bin, bout
  BitSelector #(.width(32)) bitselector_13 (.in(B), .out(Flags[2]), .sel(subtractor_6_out));
  Comparator #(.width(32)) comparator_5 (.a(SignInpout), .b({32{1'b0}}), .eq(Flags[1]), .lt(Flags[0]));  // open: gt
  BitSelector #(.width(32)) bitselector_14 (.in(SBC), .out(bitselector_14_out), .sel({5{1'b1}}));
  BitSelector #(.width(32)) bitselector_15 (.in(A), .out(bitselector_15_out), .sel({5{1'b1}}));
  BitSelector #(.width(32)) bitselector_16 (.in(B), .out(bitselector_16_out), .sel({5{1'b1}}));
  BitSelector #(.width(32)) bitselector_17 (.in(CMP), .out(bitselector_17_out), .sel({5{1'b1}}));
  BitSelector #(.width(32)) bitselector_18 (.in(A), .out(bitselector_18_out), .sel({5{1'b1}}));
  BitSelector #(.width(32)) bitselector_19 (.in(B), .out(bitselector_19_out), .sel({5{1'b1}}));
  xor xor_6 (xor_6_out, bitselector_14_out, bitselector_15_out);
  xor xor_7 (xor_7_out, bitselector_15_out, bitselector_16_out);
  xor xor_8 (xor_8_out, bitselector_17_out, bitselector_18_out);
  xor xor_9 (xor_9_out, bitselector_18_out, bitselector_19_out);
  BitSelector #(.width(32)) bitselector_20 (.in(SBC), .out(bitselector_20_out), .sel({5{1'b1}}));
  Comparator #(.width(1)) comparator_6 (
    .a(bitselector_20_out), .b(bitselector_21_out), .eq(comparator_6_eq));  // open: gt, lt
  BitSelector #(.width(32)) bitselector_21 (.in(B), .out(bitselector_21_out), .sel({5{1'b1}}));
  and and_7 (and_7_out, xor_6_out, xor_7_out);
  BitSelector #(.width(32)) bitselector_22 (.in(CMP), .out(bitselector_22_out), .sel({5{1'b1}}));
  Comparator #(.width(1)) comparator_7 (
    .a(bitselector_22_out), .b(bitselector_23_out), .eq(comparator_7_eq));  // open: gt, lt
  BitSelector #(.width(32)) bitselector_23 (.in(B), .out(bitselector_23_out), .sel({5{1'b1}}));
  and and_8 (and_8_out, xor_8_out, xor_9_out);
  and and_9 (Flags[3], comparator_6_eq, and_7_out);
  and and_10 (Flags[3], comparator_7_eq, and_8_out);

  // Other names for the same wires on the sheet: Cin = CarryIn; N = Flags[0]; Z = Flags[1]; C = Flags[2];
  //   V = Flags[3]

  // Notes on the sheet:
  //   Note: for ROR, C = N
  //   Note 2: assume that shift > 0 for LSL and LSR
  //   Constante = 0
  //   Constante = 1
  //   Constante = 0
  //   Constante = 1
  //   Carry Flag : left shift
  //   Carry Flag : right ari shift
  //   Constante = 0
  //   Carry Flag : left shift
endmodule
