// Logisim project Ctl_Opcode_Decoder.circ as structural Verilog: 1 circuit, main circuit Opcode_Decoder
module Opcode_Decoder (
  input  [5:0] Opcode,
  output Shift,
  output Data_Processing,
  output Load_Store,
  output SP_Address,
  output Conditional
);

  wire [5:1] demultiplexer_1_out0, demultiplexer_1_out3, demultiplexer_1_out6;

  Demultiplexer #(.enable("false"), .select(3), .width(6)) demultiplexer_1 (
    .out0({demultiplexer_1_out0, Shift}), .out3({demultiplexer_1_out3, Data_Processing}),
    .out6({demultiplexer_1_out6, Load_Store}), .in(Opcode));  // open: out1, out2, out4, out5, out7, sel
  // Pins of 1 and 6 bits meet at {demultiplexer_1_out0, Shift}
  // Pins of 1 and 6 bits meet at {demultiplexer_1_out3, Data_Processing}
  // Pins of 1 and 6 bits meet at {demultiplexer_1_out6, Load_Store}

  // Other names for the same wires on the sheet: OpCodeInput[5:0] = Opcode

  // Notes on the sheet:
  //   SP Address
  //   Conditional branch
  //   Shift, add, sub, mov
  //   Load/Store
  //   Data Processing
endmodule
