// Logisim project Ctl_Data_Processing.circ as structural Verilog: 1 circuit, main circuit Data_Processing
module Data_Processing (
  input  Enable,
  input  [15:0] Instruction,
  output [2:0] Rd,
  output [2:0] Rn,
  output [2:0] Rm,
  output [3:0] ALU_Opcode,
  output [3:0] Flags_Update_Mask
);

  wire [3:0] multiplexer_2_out;
  wire [15:0] Instruction_t;

  BitSelector #(.group(3), .width(16)) bitselector_1 (.in(Instruction_t), .out(Rd), .sel(3'b000));
  BitSelector #(.group(3), .width(16)) bitselector_2 (.in(Instruction_t), .out(Rm), .sel(3'b001));
  BitSelector #(.group(3), .width(16)) bitselector_3 (.in(Instruction_t), .out(ALU_Opcode[2:0]), .sel(3'b010));
  BitSelector #(.width(16)) bitselector_4 (.in(Instruction_t), .out(ALU_Opcode[3]), .sel(4'b1001));
  Multiplexer #(.enable("false"), .width(16)) multiplexer_1 (
    .in0({16{1'b0}}), .in1(Instruction), .out(Instruction_t), .sel(Enable));
  Multiplexer #(.enable("false"), .select(4), .width(4)) multiplexer_2 (
    .in0(4'b1110), .in1(4'b1110), .in2(4'b1110), .in3(4'b1110), .in4(4'b1110), .in5(4'b1111), .in6(4'b1111),
    .in7(4'b1110), .in8(4'b1110), .in9(4'b1111), .in10(4'b1111), .in11(4'b1111), .in12(4'b1110),
    .in13(4'b1100), .in14(4'b1110), .in15(4'b1110), .out(multiplexer_2_out), .sel(ALU_Opcode));
  Multiplexer #(.enable("false"), .width(4)) multiplexer_3 (
    .in0(4'b0000), .in1(multiplexer_2_out), .out(Flags_Update_Mask), .sel(Enable));

  assign Rn = Rd;

  // Other names for the same wires on the sheet: A[2:0] = Rm; B[2:0] = Rd; Opcode[3:0] = ALU_Opcode;
  //   Update_Flags[3:0] = Flags_Update_Mask

  // Notes on the sheet:
  //   Note 2: RSB instruction has Rn as 1st operand.
  //   MUL instruction has Rn as 1st operand and Rdm as 2nd operand
  //   For simplification purposes, Rm is used for 1st operand both here and in the ALU.
  //   Note: instructions that does not save the result will still have the second operand as the destination register, the ALU will copy the second register to the destination register
  //   Pull output low on Enable = 0
endmodule
